// Logisim project lambdaProcessor(dualcore).circ as structural Verilog: 2 circuits, main circuit main
module main (
);

  wire main_1_clk_, main_1_clk_out, main_1_ld, main_1_ram_sel, main_1_str;
  wire [31:0] main_1_program_addr, main_1_ram_addr, main_1_ram_data_in, ram_1_data, rom_1_data;

  lambdaCPU_v4_main main_1 (
    .clk_out(main_1_clk_out), .ram_sel(main_1_ram_sel), .str(main_1_str), .clk_(main_1_clk_), .ld(main_1_ld),
    .ram_addr(main_1_ram_addr), .ram_data_in(main_1_ram_data_in), .ram_data_out(ram_1_data),
    .program_addr(main_1_program_addr), .program_data(rom_1_data));
  RAM_part #(.addrWidth(24), .dataWidth(32), .bus("separate")) ram_1 (
    .addr(main_1_ram_addr[23:0]), .din(main_1_ram_data_in), .data(ram_1_data), .str(main_1_str),
    .sel(main_1_ram_sel), .clk(main_1_clk_), .ld(main_1_ld));  // open: clr
  ROM #(.addrWidth(24), .dataWidth(32)) rom_1 (.addr(main_1_program_addr[23:0]), .data(rom_1_data));  // open: sel

  // Notes on the sheet:
  //   contents of rom_1 (hex, n*v repeats v):
  //   34010027 34020005 22001a 1010 812 ac010000 ac020001 3c01dead 3421beef 200011 200010 ac010002
endmodule

module RAM (
  input  [31:0] Addr_in,
  input  [31:0] Data_in,
  input  [23:0] in_3,
  input  [1:0] in_4,
  input  sel,
  input  str,
  input  ld,
  input  [4:0] in_8,
  input  [31:0] in_9,
  input  in_10,
  input  in_11,
  input  [6:0] in_12,
  input  [6:0] in_13,
  input  in_14,
  input  in_15,
  input  in_16,
  output [31:0] out_17
);

  wire and_1_out, and_2_out, and_3_out, and_4_out, buffer_1_out, buffer_2_out, buffer_3_out, buffer_4_out,
       buffer_5_out, buffer_9_out, buffer_10_out, buffer_11_out, buffer_12_out, buffer_13_out, clock_1_out,
       clock_2_out, decoder_1_out0, delay_x10_1_out_2, delay_x10_2_out_2, delay_x10_3_out_2,
       delay_x10_4_out_2, delay_x10_5_out_2, keyboard_1_avail, not_1_out, not_2_out, not_3_out, not_4_out,
       or_1_out, undriven, undriven_2;
  wire [4:0] counter_3_q, multiplexer_3_out;
  wire [6:0] keyboard_1_data;
  wire [7:0] bit_extender_1_out, ram_2_data;
  wire [13:0] adder_1_out, counter_2_q, counter_4_q, multiplexer_4_out, multiplier_1_out;
  wire [15:0] not_5_out, ram_4_data;
  wire [31:0] buffer_6_out, buffer_7_out, buffer_8_out, counter_1_q, decoder_2_out0, dotmatrix_1_p3,
       multiplexer_1_out, ram_1_data, ram_3_data;

  Keyboard #(.buflen(256)) keyboard_1 (
    .clk(undriven), .re(undriven), .avail(keyboard_1_avail), .data(keyboard_1_data));  // open: clr
  Decoder #(.select(2), .disabled(0)) decoder_1 (
    .out0(decoder_1_out0), .sel(Addr_in[25:24]), .en(sel));  // open: out1, out2, out3
  and and_1 (and_1_out, decoder_1_out0, str);
  and and_2 (and_2_out, decoder_1_out0, ld);
  Counter #(.width(32), .max('hffffffff)) counter_1 (
    .count(keyboard_1_avail), .Q(counter_1_q), .clk(undriven));  // open: load, D, carry, clr
  or or_1 (or_1_out, ~keyboard_1_avail, ~undriven);  // OR_Gate
  assign bit_extender_1_out = {{1{1'b0}}, keyboard_1_data};  // Bit_Extender bit_extender_1
  RAM_part #(.addrWidth(24), .dataWidth(32), .bus("separate")) ram_1 (
    .addr(Addr_in[23:0]), .din(Data_in), .data(ram_1_data), .str(and_1_out), .sel(decoder_1_out0),
    .clk(undriven), .ld(and_2_out));  // open: clr
  Multiplexer #(.width(32), .enable("false")) multiplexer_1 (
    .in0(counter_1_q), .out(multiplexer_1_out), .sel(or_1_out));  // open: in1
  Multiplexer multiplexer_2 ();  // open: in0, in1, out, sel, en
  buf buffer_1 (buffer_1_out, buffer_2_out);
  buf buffer_2 (buffer_2_out, buffer_3_out);
  buf buffer_3 (buffer_3_out, buffer_4_out);
  buf buffer_4 (buffer_4_out, undriven);
  RAM_part #(.addrWidth(24), .bus("separate")) ram_2 (
    .addr(multiplexer_1_out[23:0]), .din(bit_extender_1_out), .data(ram_2_data), .str(keyboard_1_avail),
    .clk(buffer_1_out), .ld(undriven_2));  // open: sel, clr
  Counter #(.width(14), .max('h7f)) counter_2 (
    .count(clock_2_out), .Q(counter_2_q), .clk(clock_2_out));  // open: load, D, carry, clr
  // Probe on {{6{1'b0}}, in_4, in_3}
  Multiplier #(.width(14)) multiplier_1 (.a(counter_2_q), .b(14'h80), .out(multiplier_1_out));  // open: cin, cout
  buf buffer_5 (buffer_5_out, in_11);
  // Probe on {in_13, in_12}
  Decoder #(.select(5), .enable("false")) decoder_2 (
    .out0(decoder_2_out0[0]), .out1(decoder_2_out0[1]), .out2(decoder_2_out0[2]), .out3(decoder_2_out0[3]),
    .out4(decoder_2_out0[4]), .out5(decoder_2_out0[5]), .out6(decoder_2_out0[6]), .out7(decoder_2_out0[7]),
    .out8(decoder_2_out0[8]), .out9(decoder_2_out0[9]), .out10(decoder_2_out0[10]),
    .out11(decoder_2_out0[11]), .out12(decoder_2_out0[12]), .out13(decoder_2_out0[13]),
    .out14(decoder_2_out0[14]), .out15(decoder_2_out0[15]), .out16(decoder_2_out0[16]),
    .out17(decoder_2_out0[17]), .out18(decoder_2_out0[18]), .out19(decoder_2_out0[19]),
    .out20(decoder_2_out0[20]), .out21(decoder_2_out0[21]), .out22(decoder_2_out0[22]),
    .out23(decoder_2_out0[23]), .out24(decoder_2_out0[24]), .out25(decoder_2_out0[25]),
    .out26(decoder_2_out0[26]), .out27(decoder_2_out0[27]), .out28(decoder_2_out0[28]),
    .out29(decoder_2_out0[29]), .out30(decoder_2_out0[30]), .out31(decoder_2_out0[31]), .sel(counter_3_q));
  Counter #(.width(5), .max('h1f), .trigger("falling")) counter_3 (
    .count(buffer_5_out), .Q(counter_3_q), .clk(in_11));  // open: load, D, carry, clr
  Multiplexer #(.width(5), .enable("false")) multiplexer_3 (
    .in0(counter_3_q), .in1(in_8), .out(multiplexer_3_out), .sel(not_1_out));
  not not_1 (not_1_out, in_11);
  Adder #(.width(14)) adder_1 (.a(counter_2_q), .b(multiplier_1_out), .out(adder_1_out));  // open: cin, cout
  and and_3 (and_3_out, in_10, ~in_11);  // AND_Gate
  Clock clock_1 (.out(clock_1_out));
  assign buffer_6_out = buffer_7_out;  // Buffer buffer_6, 32 bits wide
  assign buffer_7_out = decoder_2_out0;  // Buffer buffer_7, 32 bits wide
  assign buffer_8_out = buffer_6_out;  // Buffer buffer_8, 32 bits wide
  RAM_part #(.addrWidth(5), .dataWidth(32), .bus("separate")) ram_3 (
    .addr(multiplexer_3_out), .din(in_9), .data(ram_3_data), .str(and_3_out), .clk(not_2_out), .ld(in_11));  // open: sel, clr
  not not_2 (not_2_out, delay_x10_1_out_2);
  delay_x10 delay_x10_1 (.in_1(in_11), .out_2(delay_x10_1_out_2));
  Counter #(.width(14), .max('h3fff), .trigger("falling")) counter_4 (
    .count(buffer_9_out), .Q(counter_4_q), .clk(clock_2_out));  // open: load, D, carry, clr
  buf buffer_9 (buffer_9_out, clock_2_out);
  buf buffer_10 (buffer_10_out, buffer_11_out);
  buf buffer_11 (buffer_11_out, delay_x10_2_out_2);
  delay_x10 delay_x10_2 (.in_1(in_11), .out_2(delay_x10_2_out_2));
  Multiplexer #(.width(14), .enable("false")) multiplexer_4 (
    .in0(counter_4_q), .in1(adder_1_out), .out(multiplexer_4_out), .sel(not_3_out));
  not not_3 (not_3_out, clock_2_out);
  // DotMatrix #(.inputtype("select"), .matrixcols(32), .matrixrows(32), .persist(64)) dotmatrix_1: pin names not known; wires that end beside it: clock_1_out, buffer_8_out, dotmatrix_1_p3
  Multiplexer #(.width(32), .enable("false")) multiplexer_5 (
    .in0({32{1'b0}}), .in1(ram_3_data), .out(dotmatrix_1_p3), .sel(buffer_12_out));
  buf buffer_12 (buffer_12_out, buffer_13_out);
  buf buffer_13 (buffer_13_out, buffer_10_out);
  and and_4 (and_4_out, in_16, not_4_out);
  delay_x10 delay_x10_3 (.in_1(not_4_out), .out_2(delay_x10_3_out_2));
  not not_4 (not_4_out, clock_2_out);
  Clock clock_2 (.out(clock_2_out));
  RAM_part #(.addrWidth(14), .dataWidth(16), .bus("separate")) ram_4 (
    .addr(multiplexer_4_out), .din({16{1'b1}}), .data(ram_4_data), .str(and_4_out), .sel(1'b1),
    .clk(delay_x10_3_out_2), .ld(clock_2_out));  // open: clr
  delay_x10 delay_x10_4 (.in_1(delay_x10_5_out_2), .out_2(delay_x10_4_out_2));
  delay_x10 delay_x10_5 (.in_1(clock_2_out), .out_2(delay_x10_5_out_2));
  assign not_5_out = ~ram_4_data;  // NOT_Gate not_5, 16 bits wide
  Pull_Resistor pull_resistor_1 (.node(ram_4_data));
  // LCD_Video lcd_video_1: pin names not known; wires that end beside it: in_14, delay_x10_4_out_2, in_15, multiplexer_4_out[6:0], multiplexer_4_out[13:7], not_5_out
endmodule
